# Fritzing sketch BluetoothPhoneConnection (saved by Fritzing 0.9.3b)
breadboards: 1

parts:
  Part1 = Arduino Uno (Rev3)
  Part2 = Bluetooth HC-05 Macho
  R1 = Resistor [tolerance=±5% resistance=1k package=THT]
  R2 = Resistor [tolerance=±5% resistance=1k package=THT]
  R3 = Resistor [tolerance=±5% resistance=1k package=THT]
  HC-SR04_Sensor_1 = HC-SR04 Ultrasonic Distance Sensor
  HC-SR04_Sensor_2 = HC-SR04 Ultrasonic Distance Sensor
  J1 = Basic Servo
  Part3 = HX711 Weighing Sensor Module

nets:
  N1: Part1.D8, J1.pulse
  N2: Part1.D9_PWM, HC-SR04_Sensor_1.TRIG
  N3: Part1.D10_PWM/SS, HC-SR04_Sensor_1.ECHO
  N4: Part1.D11_PWM/MOSI, HC-SR04_Sensor_2.TRIG
  N5: Part1.D12/MISO, HC-SR04_Sensor_2.ECHO
  GND: Part1.GND, Part2.GND, R1.Pin_0, HC-SR04_Sensor_1.GND, HC-SR04_Sensor_2.GND, J1.gnd, Part3.GND
  N6: Part1.D0/RX, Part2.TXD
  N7: Part1.D1/TX, R3.Pin_1
  N8: Part1.D5_PWM, Part3.DO/RX
  N9: Part1.D6_PWM, Part3.CK/TX
  VCC: Part1.5V, Part2.VCC, HC-SR04_Sensor_1.VCC, HC-SR04_Sensor_2.VCC, J1.vcc, Part3.VCC
  N10: Part2.RXD, R2.Pin_1, R3.Pin_0
  N11: R1.Pin_1, R2.Pin_0
